# Fritzing sketch bridge_circuit (saved by Fritzing 0.9.3b)
circuit board: 7.03382cm x 5.72189cm
breadboards: 1

parts:
  Part1 = Arduino Uno (Rev3)
  U1 = LM 358 Dual Op-Amp [package="DIP8 [THT]"]

nets:
  N1: Part1.GND, U1.connector3
  N2: Part1.D5_PWM, U1.connector2
  N3: Part1.5V, U1.connector7
  N4: U1.connector0, U1.connector1
